// Logisim project 7s_adder_prototype.circ as structural Verilog: 8 circuits, main circuit main
module main (
  input  in_1,
  input  in_2,
  input  in_3,
  input  in_4,
  input  in_5,
  input  in_6,
  input  in_7,
  input  in_8,
  input  in_9,
  input  in_10,
  input  in_11,
  input  in_12,
  input  in_13,
  input  in_14
);

  wire full_adder_1_b0, full_adder_1_b1, full_adder_1_b2, full_adder_1_b3, full_adder_1_b4, led2bit_1_b1,
       led2bit_1_b2, led2bit_1_b3, led2bit_1_b4, led2bit_2_b1, led2bit_2_b2, led2bit_2_b3, led2bit_2_b4;

  led2bit led2bit_1 (
    .a(in_1), .b(in_2), .c(in_3), .d(in_4), .e(in_5), .f(in_6), .g(in_7), .b1(led2bit_1_b1),
    .b2(led2bit_1_b2), .b3(led2bit_1_b3), .b4(led2bit_1_b4));
  led2bit led2bit_2 (
    .a(in_8), .b(in_9), .c(in_10), .d(in_11), .e(in_12), .f(in_13), .g(in_14), .b1(led2bit_2_b1),
    .b2(led2bit_2_b2), .b3(led2bit_2_b3), .b4(led2bit_2_b4));
  LED led_1 (.in(full_adder_1_b4));
  full_adder full_adder_1 (
    .b11(led2bit_1_b1), .b12(led2bit_1_b2), .b13(led2bit_1_b3), .b14(led2bit_1_b4), .b21(led2bit_2_b1),
    .b22(led2bit_2_b2), .b23(led2bit_2_b3), .b24(led2bit_2_b4), .b4(full_adder_1_b4), .b3(full_adder_1_b3),
    .b2(full_adder_1_b2), .b1(full_adder_1_b1), .b0(full_adder_1_b0));
  LED led_2 (.in(full_adder_1_b3));
  LED led_3 (.in(full_adder_1_b2));
  LED led_4 (.in(full_adder_1_b0));
  LED led_5 (.in(full_adder_1_b1));
endmodule

module raw_led2bit (
  input  a,
  input  b,
  input  c,
  input  d,
  input  e,
  input  f,
  input  g,
  output b1,
  output b2,
  output b3,
  output b4
);

  wire and_2_out, and_3_out, and_4_out, and_5_out, and_6_out, and_7_out, and_8_out, and_9_out, and_10_out,
       and_11_out, and_12_out, and_13_out, and_14_out, not_1_out, not_2_out, not_3_out, not_4_out, not_5_out,
       not_6_out, not_7_out, not_8_out, not_9_out, not_10_out, not_11_out, not_12_out, not_13_out,
       not_14_out, not_15_out, not_16_out, not_17_out, not_18_out, not_19_out, not_20_out, not_21_out,
       not_22_out, not_23_out, not_24_out, not_25_out, not_26_out, not_27_out, not_28_out, not_29_out,
       not_30_out, not_31_out, not_32_out;

  and and_1 (b1, a, b, c, d, f, g);
  not not_1 (not_1_out, a);
  not not_2 (not_2_out, e);
  not not_3 (not_3_out, g);
  not not_4 (not_4_out, c);
  not not_5 (not_5_out, d);
  not not_6 (not_6_out, f);
  not not_7 (not_7_out, b);
  not not_8 (not_8_out, e);
  not not_9 (not_9_out, g);
  not not_10 (not_10_out, c);
  not not_11 (not_11_out, b);
  not not_12 (not_12_out, f);
  not not_13 (not_13_out, b);
  not not_14 (not_14_out, e);
  not not_15 (not_15_out, c);
  not not_16 (not_16_out, b);
  not not_17 (not_17_out, e);
  not not_18 (not_18_out, g);
  not not_19 (not_19_out, a);
  not not_20 (not_20_out, b);
  not not_21 (not_21_out, d);
  not not_22 (not_22_out, e);
  not not_23 (not_23_out, g);
  not not_24 (not_24_out, b);
  not not_25 (not_25_out, e);
  not not_26 (not_26_out, c);
  not not_27 (not_27_out, d);
  not not_28 (not_28_out, f);
  not not_29 (not_29_out, b);
  not not_30 (not_30_out, e);
  not not_31 (not_31_out, g);
  not not_32 (not_32_out, e);
  and and_2 (and_2_out, not_1_out, b, c, d, not_2_out, f, not_3_out);
  and and_3 (and_3_out, a, b, not_4_out, not_5_out, e, not_6_out, g);
  and and_4 (and_4_out, a, not_7_out, c, d, not_8_out, f, not_9_out);
  and and_5 (and_5_out, a, b, not_10_out, d, e, f, g);
  and and_6 (and_6_out, a, not_11_out, c, d, e, not_12_out, g);
  and and_7 (and_7_out, a, not_13_out, c, d, not_14_out, f, g);
  and and_8 (and_8_out, a, b, not_15_out, d, e, f, g);
  and and_9 (and_9_out, a, not_16_out, c, d, not_17_out, f, not_18_out);
  and and_10 (and_10_out, not_19_out, not_20_out, c, not_21_out, not_22_out, f, not_23_out);
  and and_11 (and_11_out, a, not_24_out, c, d, not_25_out, f, g);
  and and_12 (and_12_out, a, b, not_26_out, not_27_out, e, not_28_out, g);
  and and_13 (and_13_out, a, not_29_out, c, d, not_30_out, f, not_31_out);
  and and_14 (and_14_out, a, b, c, d, not_32_out, f, g);
  or or_1 (b2, and_2_out, and_3_out, and_4_out, and_5_out);
  or or_2 (b3, and_6_out, and_7_out, and_8_out, and_9_out);
  or or_3 (b4, and_10_out, and_11_out, and_12_out, and_13_out, and_14_out);
endmodule

module led2bit (
  input  a,
  input  b,
  input  c,
  input  d,
  input  e,
  input  f,
  input  g,
  output b1,
  output b2,
  output b3,
  output b4
);

  wire and_1_out, and_2_out, and_3_out, and_4_out, and_5_out, and_6_out, and_7_out, and_8_out, and_9_out,
       and_10_out, and_11_out, and_12_out, and_13_out, and_15_out, and_16_out, and_17_out, and_18_out,
       and_19_out, and_20_out, and_21_out, and_22_out, and_23_out, and_24_out, and_25_out, and_26_out,
       and_27_out, and_28_out, and_29_out, and_30_out, and_31_out, and_32_out, and_33_out, and_34_out,
       and_35_out, and_37_out, and_38_out, and_39_out, and_40_out, not_1_out, not_2_out, not_3_out,
       not_4_out, not_5_out, not_6_out, not_7_out, not_8_out, not_9_out, not_10_out, not_11_out, not_12_out,
       not_13_out, not_14_out, not_15_out, or_1_out, or_2_out, or_3_out, or_4_out, xor_1_out;

  and and_1 (and_1_out, a, b);
  and and_2 (and_2_out, d, f);
  not not_1 (not_1_out, a);
  not not_2 (not_2_out, b);
  or or_1 (or_1_out, b, c);
  not not_3 (not_3_out, b);
  not not_4 (not_4_out, d);
  not not_5 (not_5_out, g);
  and and_3 (and_3_out, and_1_out, c);
  and and_4 (and_4_out, and_2_out, g);
  and and_5 (and_5_out, not_1_out, b);
  and and_6 (and_6_out, a, not_2_out);
  not not_6 (not_6_out, d);
  and and_7 (and_7_out, d, xor_1_out);
  xor xor_1 (xor_1_out, e, f);
  not not_7 (not_7_out, d);
  and and_8 (and_8_out, not_7_out, not_8_out);
  not not_8 (not_8_out, e);
  and and_9 (and_9_out, f, not_9_out);
  not not_9 (not_9_out, g);
  and and_10 (and_10_out, a, d);
  and and_11 (and_11_out, g, or_1_out);
  and and_12 (and_12_out, not_3_out, c);
  and and_13 (and_13_out, not_4_out, not_5_out);
  and and_14 (b1, and_3_out, and_4_out);
  not not_10 (not_10_out, e);
  and and_15 (and_15_out, and_5_out, d);
  and and_16 (and_16_out, and_6_out, not_6_out);
  and and_17 (and_17_out, and_7_out, g);
  and and_18 (and_18_out, and_8_out, and_9_out);
  not not_11 (not_11_out, c);
  not not_12 (not_12_out, e);
  and and_19 (and_19_out, and_10_out, and_11_out);
  and and_20 (and_20_out, and_12_out, and_13_out);
  and and_21 (and_21_out, c, not_10_out);
  not not_13 (not_13_out, g);
  or or_2 (or_2_out, and_15_out, and_16_out);
  and and_22 (and_22_out, a, b);
  not not_14 (not_14_out, c);
  and and_23 (and_23_out, d, f);
  not not_15 (not_15_out, b);
  or or_3 (or_3_out, and_17_out, and_18_out);
  and and_24 (and_24_out, a, b);
  and and_25 (and_25_out, not_11_out, d);
  and and_26 (and_26_out, e, f);
  and and_27 (and_27_out, not_12_out, f);
  or or_4 (or_4_out, and_19_out, and_20_out);
  and and_28 (and_28_out, and_21_out, f);
  and and_29 (and_29_out, not_13_out, or_2_out);
  and and_30 (and_30_out, and_22_out, not_14_out);
  and and_31 (and_31_out, and_23_out, g);
  and and_32 (and_32_out, a, not_15_out);
  and and_33 (and_33_out, c, or_3_out);
  and and_34 (and_34_out, and_24_out, and_25_out);
  and and_35 (and_35_out, and_26_out, g);
  and and_36 (b4, and_27_out, or_4_out);
  and and_37 (and_37_out, and_28_out, and_29_out);
  and and_38 (and_38_out, and_30_out, and_31_out);
  and and_39 (and_39_out, and_32_out, and_33_out);
  and and_40 (and_40_out, and_34_out, and_35_out);
  or or_5 (b2, and_37_out, and_38_out);
  or or_6 (b3, and_39_out, and_40_out);
endmodule

module raw_bit2led (
  input  a,
  input  b,
  input  c,
  input  d,
  input  e,
  output s0,
  output s1,
  output s2,
  output s3,
  output s4,
  output s5,
  output s6,
  output s7
);

  wire and_1_out, and_2_out, and_3_out, and_4_out, and_5_out, and_6_out, and_7_out, and_8_out, and_9_out,
       and_10_out, and_11_out, and_12_out, and_13_out, and_14_out, and_15_out, and_16_out, and_17_out,
       and_18_out, and_19_out, and_20_out, and_21_out, and_22_out, and_23_out, and_24_out, and_25_out,
       and_26_out, and_27_out, and_28_out, and_29_out, and_30_out, and_31_out, and_32_out, and_33_out,
       and_34_out, and_35_out, and_36_out, and_37_out, and_38_out, and_39_out, and_40_out, and_41_out,
       and_42_out, and_43_out, and_44_out, and_45_out, and_46_out, and_47_out, and_48_out, and_49_out,
       and_50_out, and_51_out, and_52_out, and_53_out, and_54_out, and_55_out, and_56_out, and_57_out,
       and_58_out, and_59_out, and_60_out, and_61_out, and_62_out, and_63_out, and_64_out, and_65_out,
       and_66_out, and_67_out, and_68_out, and_69_out, and_70_out, and_71_out, and_72_out, and_73_out,
       and_74_out, and_75_out, and_76_out, and_77_out, and_78_out, and_79_out, and_80_out, and_81_out,
       and_82_out, and_83_out, and_84_out, and_85_out, and_86_out, and_87_out, and_88_out, and_89_out,
       and_90_out, and_91_out, and_92_out, and_93_out, and_94_out, and_95_out, and_96_out, and_97_out,
       and_98_out, and_99_out, and_100_out, and_101_out, and_102_out, and_103_out, and_104_out, and_105_out,
       and_106_out, and_107_out, and_108_out, and_109_out, and_110_out, and_111_out, and_112_out,
       and_113_out, and_114_out, not_1_out, not_2_out, not_3_out, not_4_out, not_5_out, not_6_out, not_7_out,
       not_8_out, not_9_out, not_10_out, not_11_out, not_12_out, not_13_out, not_14_out, not_15_out,
       not_16_out, not_17_out, not_18_out, not_19_out, not_20_out, not_21_out, not_22_out, not_23_out,
       not_24_out, not_25_out, not_26_out, not_27_out, not_28_out, not_29_out, not_30_out, not_31_out,
       not_32_out, not_33_out, not_34_out, not_35_out, not_36_out, not_37_out, not_38_out, not_39_out,
       not_40_out, not_41_out, not_42_out, not_43_out, not_44_out, not_45_out, not_46_out, not_47_out,
       not_48_out, not_49_out, not_50_out, not_51_out, not_52_out, not_53_out, not_54_out, not_55_out,
       not_56_out, not_57_out, not_58_out, not_59_out, not_60_out, not_61_out, not_62_out, not_63_out,
       not_64_out, not_65_out, not_66_out, not_67_out, not_68_out, not_69_out, not_70_out, not_71_out,
       not_72_out, not_73_out, not_74_out, not_75_out, not_76_out, not_77_out, not_78_out, not_79_out,
       not_80_out, not_81_out, not_82_out, not_83_out, not_84_out, not_85_out, not_86_out, not_87_out,
       not_88_out, not_89_out, not_90_out, not_91_out, not_92_out, not_93_out, not_94_out, not_95_out,
       not_96_out, not_97_out, not_98_out, not_99_out, not_100_out, not_101_out, not_102_out, not_103_out,
       not_104_out, not_105_out, not_106_out, not_107_out, not_108_out, not_109_out, not_110_out,
       not_111_out, not_112_out, not_113_out, or_1_out, or_2_out, or_3_out, or_4_out, or_5_out, or_6_out,
       or_7_out, or_8_out, or_9_out, or_10_out, or_11_out, or_12_out, or_13_out, or_14_out, or_15_out,
       or_16_out, or_17_out, or_18_out, or_19_out, or_21_out, or_22_out, or_23_out, or_24_out, or_25_out,
       or_26_out, or_27_out, or_28_out, or_30_out, or_31_out, or_32_out, or_33_out;

  not not_1 (not_1_out, a);
  not not_2 (not_2_out, a);
  not not_3 (not_3_out, b);
  not not_4 (not_4_out, c);
  not not_5 (not_5_out, d);
  not not_6 (not_6_out, b);
  not not_7 (not_7_out, c);
  not not_8 (not_8_out, e);
  not not_9 (not_9_out, a);
  not not_10 (not_10_out, b);
  not not_11 (not_11_out, a);
  not not_12 (not_12_out, a);
  not not_13 (not_13_out, c);
  not not_14 (not_14_out, b);
  not not_15 (not_15_out, c);
  not not_16 (not_16_out, d);
  not not_17 (not_17_out, a);
  not not_18 (not_18_out, b);
  not not_19 (not_19_out, d);
  not not_20 (not_20_out, a);
  not not_21 (not_21_out, c);
  not not_22 (not_22_out, d);
  not not_23 (not_23_out, a);
  not not_24 (not_24_out, b);
  not not_25 (not_25_out, c);
  not not_26 (not_26_out, e);
  not not_27 (not_27_out, a);
  not not_28 (not_28_out, b);
  not not_29 (not_29_out, d);
  not not_30 (not_30_out, e);
  not not_31 (not_31_out, a);
  not not_32 (not_32_out, b);
  not not_33 (not_33_out, e);
  not not_34 (not_34_out, a);
  not not_35 (not_35_out, d);
  not not_36 (not_36_out, a);
  not not_37 (not_37_out, b);
  not not_38 (not_38_out, a);
  not not_39 (not_39_out, a);
  not not_40 (not_40_out, b);
  not not_41 (not_41_out, c);
  not not_42 (not_42_out, d);
  not not_43 (not_43_out, a);
  not not_44 (not_44_out, b);
  not not_45 (not_45_out, c);
  not not_46 (not_46_out, a);
  not not_47 (not_47_out, a);
  not not_48 (not_48_out, b);
  not not_49 (not_49_out, c);
  not not_50 (not_50_out, e);
  not not_51 (not_51_out, a);
  not not_52 (not_52_out, b);
  not not_53 (not_53_out, e);
  not not_54 (not_54_out, a);
  not not_55 (not_55_out, c);
  not not_56 (not_56_out, a);
  not not_57 (not_57_out, d);
  not not_58 (not_58_out, e);
  not not_59 (not_59_out, b);
  not not_60 (not_60_out, c);
  not not_61 (not_61_out, b);
  not not_62 (not_62_out, c);
  not not_63 (not_63_out, a);
  not not_64 (not_64_out, b);
  not not_65 (not_65_out, a);
  not not_66 (not_66_out, a);
  not not_67 (not_67_out, b);
  not not_68 (not_68_out, c);
  not not_69 (not_69_out, a);
  not not_70 (not_70_out, d);
  not not_71 (not_71_out, a);
  not not_72 (not_72_out, b);
  not not_73 (not_73_out, e);
  not not_74 (not_74_out, a);
  not not_75 (not_75_out, a);
  not not_76 (not_76_out, c);
  not not_77 (not_77_out, a);
  and and_1 (and_1_out, not_1_out, b);
  and and_2 (and_2_out, not_2_out, b);
  and and_3 (and_3_out, a, not_3_out);
  and and_4 (and_4_out, not_4_out, not_5_out);
  and and_5 (and_5_out, a, not_6_out);
  and and_6 (and_6_out, not_7_out, not_8_out);
  and and_7 (and_7_out, not_9_out, not_10_out);
  and and_8 (and_8_out, not_11_out, c);
  not not_78 (not_78_out, a);
  and and_9 (and_9_out, not_12_out, not_13_out);
  not not_79 (not_79_out, e);
  and and_10 (and_10_out, a, not_14_out);
  and and_11 (and_11_out, not_15_out, not_16_out);
  not not_80 (not_80_out, b);
  not not_81 (not_81_out, c);
  and and_12 (and_12_out, not_17_out, not_18_out);
  and and_13 (and_13_out, c, not_19_out);
  and and_14 (and_14_out, not_20_out, b);
  and and_15 (and_15_out, not_21_out, not_22_out);
  and and_16 (and_16_out, not_23_out, b);
  and and_17 (and_17_out, c, d);
  and and_18 (and_18_out, a, not_24_out);
  and and_19 (and_19_out, not_25_out, not_26_out);
  and and_20 (and_20_out, not_27_out, not_28_out);
  and and_21 (and_21_out, not_29_out, not_30_out);
  and and_22 (and_22_out, not_31_out, not_32_out);
  and and_23 (and_23_out, c, not_33_out);
  not not_82 (not_82_out, a);
  not not_83 (not_83_out, c);
  not not_84 (not_84_out, e);
  and and_24 (and_24_out, not_34_out, not_35_out);
  not not_85 (not_85_out, e);
  and and_25 (and_25_out, not_36_out, not_37_out);
  and and_26 (and_26_out, d, e);
  not not_86 (not_86_out, a);
  not not_87 (not_87_out, c);
  and and_27 (and_27_out, not_38_out, b);
  not not_88 (not_88_out, d);
  and and_28 (and_28_out, not_39_out, b);
  not not_89 (not_89_out, e);
  and and_29 (and_29_out, not_40_out, not_41_out);
  and and_30 (and_30_out, not_42_out, e);
  not not_90 (not_90_out, b);
  not not_91 (not_91_out, c);
  not not_92 (not_92_out, e);
  and and_31 (and_31_out, not_43_out, not_44_out);
  and and_32 (and_32_out, not_45_out, d);
  and and_33 (and_33_out, not_46_out, c);
  not not_93 (not_93_out, d);
  not not_94 (not_94_out, a);
  and and_34 (and_34_out, not_47_out, b);
  and and_35 (and_35_out, a, not_48_out);
  and and_36 (and_36_out, not_49_out, not_50_out);
  not not_95 (not_95_out, a);
  and and_37 (and_37_out, not_51_out, not_52_out);
  and and_38 (and_38_out, d, not_53_out);
  and and_39 (and_39_out, not_54_out, not_55_out);
  not not_96 (not_96_out, e);
  and and_40 (and_40_out, not_56_out, b);
  and and_41 (and_41_out, not_57_out, not_58_out);
  and and_42 (and_42_out, not_59_out, not_60_out);
  not not_97 (not_97_out, e);
  not not_98 (not_98_out, a);
  and and_43 (and_43_out, not_61_out, not_62_out);
  not not_99 (not_99_out, d);
  not not_100 (not_100_out, b);
  not not_101 (not_101_out, c);
  not not_102 (not_102_out, e);
  and and_44 (and_44_out, not_63_out, not_64_out);
  and and_45 (and_45_out, not_65_out, b);
  not not_103 (not_103_out, c);
  not not_104 (not_104_out, a);
  and and_46 (and_46_out, not_66_out, not_67_out);
  and and_47 (and_47_out, not_68_out, d);
  and and_48 (and_48_out, not_69_out, c);
  and and_49 (and_49_out, not_70_out, e);
  and and_50 (and_50_out, not_71_out, not_72_out);
  and and_51 (and_51_out, d, not_73_out);
  and and_52 (and_52_out, not_74_out, b);
  not not_105 (not_105_out, d);
  and and_53 (and_53_out, not_75_out, not_76_out);
  not not_106 (not_106_out, e);
  and and_54 (and_54_out, not_77_out, b);
  and and_55 (and_55_out, c, e);
  not not_107 (not_107_out, b);
  not not_108 (not_108_out, c);
  and and_56 (and_56_out, and_1_out, d);
  or or_1 (or_1_out, and_56_out, and_57_out);
  and and_57 (and_57_out, and_2_out, c);
  and and_58 (and_58_out, and_3_out, and_4_out);
  or or_2 (or_2_out, and_58_out, and_59_out);
  and and_59 (and_59_out, and_5_out, and_6_out);
  and and_60 (and_60_out, and_7_out, d);
  or or_3 (or_3_out, and_60_out, and_61_out);
  and and_61 (and_61_out, and_8_out, e);
  and and_62 (and_62_out, not_78_out, b);
  and and_63 (and_63_out, and_62_out, not_109_out);
  not not_109 (not_109_out, d);
  and and_64 (and_64_out, and_9_out, not_79_out);
  or or_4 (or_4_out, and_64_out, and_65_out);
  and and_65 (and_65_out, and_10_out, and_11_out);
  and and_66 (and_66_out, not_80_out, not_81_out);
  and and_67 (and_67_out, and_66_out, not_110_out);
  not not_110 (not_110_out, e);
  and and_68 (and_68_out, and_12_out, and_13_out);
  or or_5 (or_5_out, and_68_out, and_69_out);
  and and_69 (and_69_out, and_14_out, and_15_out);
  and and_70 (and_70_out, and_16_out, and_17_out);
  or or_6 (or_6_out, and_70_out, and_71_out);
  and and_71 (and_71_out, and_18_out, and_19_out);
  and and_72 (and_72_out, and_20_out, and_21_out);
  or or_7 (or_7_out, and_72_out, and_73_out);
  and and_73 (and_73_out, and_22_out, and_23_out);
  and and_74 (and_74_out, not_82_out, b);
  and and_75 (and_75_out, and_74_out, and_76_out);
  and and_76 (and_76_out, not_83_out, not_84_out);
  and and_77 (and_77_out, and_24_out, not_85_out);
  or or_8 (or_8_out, and_77_out, and_78_out);
  and and_78 (and_78_out, and_25_out, and_26_out);
  and and_79 (and_79_out, not_86_out, not_87_out);
  or or_9 (or_9_out, and_79_out, and_80_out);
  and and_80 (and_80_out, and_27_out, not_88_out);
  and and_81 (and_81_out, and_28_out, not_89_out);
  or or_10 (or_10_out, and_81_out, and_82_out);
  and and_82 (and_82_out, and_29_out, and_30_out);
  and and_83 (and_83_out, not_90_out, not_91_out);
  and and_84 (and_84_out, and_83_out, and_85_out);
  and and_85 (and_85_out, d, not_92_out);
  and and_86 (and_86_out, and_31_out, and_32_out);
  or or_11 (or_11_out, and_86_out, and_87_out);
  and and_87 (and_87_out, and_33_out, not_93_out);
  and and_88 (and_88_out, not_94_out, b);
  and and_89 (and_89_out, and_88_out, not_111_out);
  not not_111 (not_111_out, d);
  and and_90 (and_90_out, and_34_out, c);
  or or_12 (or_12_out, and_90_out, and_91_out);
  and and_91 (and_91_out, and_35_out, and_36_out);
  and and_92 (and_92_out, not_95_out, c);
  and and_93 (and_93_out, and_92_out, not_112_out);
  not not_112 (not_112_out, e);
  and and_94 (and_94_out, and_37_out, and_38_out);
  or or_13 (or_13_out, and_94_out, and_95_out);
  and and_95 (and_95_out, and_39_out, not_96_out);
  and and_96 (and_96_out, and_40_out, and_41_out);
  or or_14 (or_14_out, and_96_out, and_97_out);
  and and_97 (and_97_out, and_42_out, not_97_out);
  and and_98 (and_98_out, not_98_out, e);
  or or_15 (or_15_out, and_98_out, and_99_out);
  and and_99 (and_99_out, and_43_out, not_99_out);
  and and_100 (and_100_out, a, not_100_out);
  and and_101 (and_101_out, and_100_out, and_102_out);
  and and_102 (and_102_out, not_101_out, not_102_out);
  and and_103 (and_103_out, and_44_out, c);
  or or_16 (or_16_out, and_103_out, and_104_out);
  and and_104 (and_104_out, and_45_out, not_103_out);
  and and_105 (and_105_out, not_104_out, c);
  and and_106 (and_106_out, and_105_out, d);
  and and_107 (and_107_out, and_46_out, and_47_out);
  or or_17 (or_17_out, and_107_out, and_108_out);
  and and_108 (and_108_out, and_48_out, and_49_out);
  and and_109 (and_109_out, and_50_out, and_51_out);
  or or_18 (or_18_out, and_109_out, and_110_out);
  and and_110 (and_110_out, and_52_out, not_105_out);
  and and_111 (and_111_out, and_53_out, not_106_out);
  or or_19 (or_19_out, and_111_out, and_112_out);
  and and_112 (and_112_out, and_54_out, and_55_out);
  and and_113 (and_113_out, not_107_out, not_108_out);
  and and_114 (and_114_out, and_113_out, not_113_out);
  not not_113 (not_113_out, e);
  or or_20 (s0, or_1_out, or_2_out);
  or or_21 (or_21_out, or_3_out, and_63_out);
  or or_22 (or_22_out, or_4_out, and_67_out);
  or or_23 (or_23_out, or_5_out, or_6_out);
  or or_24 (or_24_out, or_7_out, and_75_out);
  or or_25 (or_25_out, or_8_out, or_9_out);
  or or_26 (or_26_out, or_10_out, and_84_out);
  or or_27 (or_27_out, or_11_out, and_89_out);
  or or_28 (or_28_out, or_12_out, and_93_out);
  or or_29 (s5, or_13_out, or_14_out);
  or or_30 (or_30_out, or_15_out, and_101_out);
  or or_31 (or_31_out, or_16_out, and_106_out);
  or or_32 (or_32_out, or_17_out, or_18_out);
  or or_33 (or_33_out, or_19_out, and_114_out);
  or or_34 (s1, or_21_out, or_22_out);
  or or_35 (s2, or_23_out, or_24_out);
  or or_36 (s3, or_25_out, or_26_out);
  or or_37 (s4, or_27_out, or_28_out);
  or or_38 (s6, or_30_out, or_31_out);
  or or_39 (s7, or_32_out, or_33_out);
endmodule

module bit2led (
  input  a,
  input  b,
  input  c,
  input  d,
  input  e,
  output s0,
  output s1,
  output s2,
  output s3,
  output s4,
  output s5,
  output s6,
  output s7
);

  wire and_1_out, and_2_out, and_3_out, and_4_out, and_5_out, and_6_out, and_7_out, and_8_out, and_9_out,
       and_10_out, and_11_out, and_12_out, and_13_out, and_14_out, and_15_out, and_16_out, and_17_out,
       and_18_out, and_19_out, and_20_out, and_21_out, and_22_out, and_23_out, and_24_out, and_25_out,
       and_26_out, and_27_out, and_28_out, and_29_out, and_30_out, and_31_out, and_32_out, nand_1_out,
       not_1_out, not_2_out, not_3_out, not_4_out, not_5_out, not_6_out, not_7_out, not_8_out, not_9_out,
       not_10_out, not_11_out, not_12_out, not_13_out, not_14_out, not_15_out, not_16_out, not_17_out,
       not_18_out, not_19_out, not_20_out, not_21_out, not_22_out, not_23_out, not_24_out, not_25_out,
       not_26_out, not_27_out, not_28_out, not_29_out, not_30_out, not_31_out, not_32_out, not_33_out,
       not_34_out, not_35_out, not_36_out, not_37_out, not_38_out, not_39_out, not_40_out, not_41_out,
       not_42_out, not_43_out, not_44_out, not_45_out, not_46_out, or_1_out, or_2_out, or_3_out, or_4_out,
       or_5_out, or_6_out, or_7_out, or_8_out, or_9_out, or_10_out, or_11_out, or_12_out, or_13_out,
       or_16_out, or_18_out, or_19_out, or_20_out, xnor_1_out, xnor_2_out, xor_1_out, xor_2_out, xor_3_out,
       xor_4_out, xor_5_out, xor_6_out, xor_7_out;

  not not_1 (not_1_out, d);
  not not_2 (not_2_out, e);
  not not_3 (not_3_out, d);
  nand nand_1 (nand_1_out, d, e);
  not not_4 (not_4_out, d);
  not not_5 (not_5_out, e);
  not not_6 (not_6_out, d);
  not not_7 (not_7_out, e);
  and and_1 (and_1_out, d, e);
  not not_8 (not_8_out, e);
  xor xor_1 (xor_1_out, b, d);
  not not_9 (not_9_out, c);
  not not_10 (not_10_out, e);
  not not_11 (not_11_out, b);
  not not_12 (not_12_out, a);
  or or_1 (or_1_out, d, c);
  not not_13 (not_13_out, b);
  not not_14 (not_14_out, c);
  or or_2 (or_2_out, not_1_out, not_2_out);
  xor xor_2 (xor_2_out, b, d);
  xnor xnor_1 (xnor_1_out, c, e);
  and and_2 (and_2_out, a, not_3_out);
  not not_15 (not_15_out, e);
  and and_3 (and_3_out, c, nand_1_out);
  and and_4 (and_4_out, not_4_out, not_5_out);
  not not_16 (not_16_out, c);
  and and_5 (and_5_out, not_6_out, not_7_out);
  xor xor_3 (xor_3_out, b, and_1_out);
  not not_17 (not_17_out, d);
  or or_3 (or_3_out, c, b);
  or or_4 (or_4_out, b, not_8_out);
  not not_18 (not_18_out, a);
  not not_19 (not_19_out, e);
  not not_20 (not_20_out, a);
  or or_5 (or_5_out, xor_1_out, not_9_out);
  not not_21 (not_21_out, b);
  not not_22 (not_22_out, c);
  xor xor_4 (xor_4_out, b, c);
  and and_6 (and_6_out, c, d);
  and and_7 (and_7_out, a, not_10_out);
  not not_23 (not_23_out, d);
  and and_8 (and_8_out, not_11_out, d);
  and and_9 (and_9_out, c, e);
  not not_24 (not_24_out, d);
  and and_10 (and_10_out, not_12_out, b, or_1_out);
  and and_11 (and_11_out, a, not_13_out, not_14_out, or_2_out);
  not not_25 (not_25_out, a);
  and and_12 (and_12_out, not_25_out, or_6_out);
  or or_6 (or_6_out, xor_2_out, xnor_1_out);
  not not_26 (not_26_out, b);
  not not_27 (not_27_out, c);
  and and_13 (and_13_out, not_26_out, not_27_out, or_7_out);
  or or_7 (or_7_out, and_2_out, not_15_out);
  not not_28 (not_28_out, b);
  or or_8 (or_8_out, and_3_out, and_4_out);
  xnor xnor_2 (xnor_2_out, c, d);
  not not_29 (not_29_out, a);
  or or_9 (or_9_out, not_16_out, and_5_out, xor_3_out);
  not not_30 (not_30_out, b);
  not not_31 (not_31_out, c);
  xor xor_5 (xor_5_out, d, e);
  not not_32 (not_32_out, a);
  and and_14 (and_14_out, not_17_out, or_3_out);
  or or_10 (or_10_out, and_14_out, and_15_out);
  and and_15 (and_15_out, c, or_4_out);
  not not_33 (not_33_out, b);
  not not_34 (not_34_out, c);
  and and_16 (and_16_out, not_18_out, d);
  or or_11 (or_11_out, and_16_out, and_17_out);
  and and_17 (and_17_out, a, not_19_out);
  and and_18 (and_18_out, not_20_out, or_5_out);
  and and_19 (and_19_out, not_21_out, not_22_out);
  not not_35 (not_35_out, a);
  and and_20 (and_20_out, not_35_out, or_12_out);
  or or_12 (or_12_out, xor_4_out, and_6_out, e);
  not not_36 (not_36_out, b);
  not not_37 (not_37_out, c);
  and and_21 (and_21_out, not_36_out, not_37_out, or_13_out);
  or or_13 (or_13_out, and_7_out, not_23_out);
  not not_38 (not_38_out, a);
  not not_39 (not_39_out, b);
  xor xor_6 (xor_6_out, and_8_out, and_9_out);
  and and_22 (and_22_out, b, not_24_out);
  or or_14 (s0, and_10_out, and_11_out);
  or or_15 (s1, and_12_out, and_13_out);
  and and_23 (and_23_out, not_28_out, or_8_out);
  and and_24 (and_24_out, b, xnor_2_out);
  and and_25 (and_25_out, not_29_out, or_9_out);
  and and_26 (and_26_out, not_30_out, not_31_out, xor_5_out);
  and and_27 (and_27_out, not_32_out, or_10_out);
  and and_28 (and_28_out, not_33_out, not_34_out, or_11_out);
  not not_40 (not_40_out, e);
  or or_16 (or_16_out, and_18_out, and_19_out);
  or or_17 (s6, and_20_out, and_21_out);
  or or_18 (or_18_out, not_38_out, not_39_out);
  not not_41 (not_41_out, c);
  and and_29 (and_29_out, or_18_out, not_41_out, not_42_out);
  not not_42 (not_42_out, e);
  not not_43 (not_43_out, a);
  and and_30 (and_30_out, not_43_out, or_19_out);
  or or_19 (or_19_out, xor_6_out, and_22_out);
  not not_44 (not_44_out, a);
  and and_31 (and_31_out, not_44_out, or_20_out);
  or or_20 (or_20_out, and_23_out, and_24_out);
  xor xor_7 (xor_7_out, a, b);
  not not_45 (not_45_out, c);
  and and_32 (and_32_out, xor_7_out, not_45_out, not_46_out);
  not not_46 (not_46_out, e);
  or or_21 (s3, and_25_out, and_26_out);
  or or_22 (s4, and_27_out, and_28_out);
  and and_33 (s5, not_40_out, or_16_out);
  or or_23 (s7, and_29_out, and_30_out);
  or or_24 (s2, and_31_out, and_32_out);
endmodule

module minecraft_preview (
  input  a,
  input  b,
  input  c,
  input  d,
  input  e,
  input  f,
  input  g,
  output b1,
  output b2,
  output b3,
  output b4
);

  wire and_1_out, and_2_out, and_3_out, and_4_out, and_5_out, and_6_out, and_7_out, and_8_out, and_9_out,
       and_10_out, and_11_out, and_12_out, and_13_out, and_14_out, and_16_out, and_17_out, and_18_out,
       and_19_out, and_20_out, and_21_out, and_22_out, and_23_out, and_24_out, and_25_out, and_26_out,
       and_27_out, and_28_out, and_29_out, and_30_out, and_31_out, and_32_out, and_33_out, and_34_out,
       and_35_out, and_36_out, and_37_out, and_38_out, and_39_out, and_40_out, and_41_out, and_42_out,
       and_43_out, and_44_out, and_45_out, and_46_out, not_1_out, not_2_out, not_3_out, not_4_out, not_5_out,
       not_6_out, not_7_out, not_8_out, not_9_out, not_10_out, not_11_out, not_12_out, not_13_out,
       not_14_out, not_15_out, not_16_out, not_17_out, not_18_out, not_19_out, not_20_out, or_1_out,
       or_2_out, or_3_out, or_4_out, or_5_out, or_6_out;

  and and_1 (and_1_out, a, b);
  and and_2 (and_2_out, d, f);
  not not_1 (not_1_out, d);
  not not_2 (not_2_out, f);
  not not_3 (not_3_out, a);
  not not_4 (not_4_out, b);
  not not_5 (not_5_out, f);
  not not_6 (not_6_out, c);
  not not_7 (not_7_out, d);
  not not_8 (not_8_out, f);
  not not_9 (not_9_out, e);
  not not_10 (not_10_out, a);
  not not_11 (not_11_out, d);
  and and_3 (and_3_out, and_1_out, c);
  and and_4 (and_4_out, and_2_out, g);
  and and_5 (and_5_out, not_1_out, not_2_out);
  and and_6 (and_6_out, d, f);
  and and_7 (and_7_out, not_3_out, b);
  and and_8 (and_8_out, a, not_4_out);
  and and_9 (and_9_out, e, not_5_out);
  not not_12 (not_12_out, e);
  not not_13 (not_13_out, c);
  and and_10 (and_10_out, not_6_out, not_7_out);
  and and_11 (and_11_out, e, not_8_out);
  and and_12 (and_12_out, c, d);
  and and_13 (and_13_out, not_9_out, f);
  and and_14 (and_14_out, not_10_out, not_11_out);
  not not_14 (not_14_out, g);
  and and_15 (b1, and_3_out, and_4_out);
  and and_16 (and_16_out, and_5_out, g);
  and and_17 (and_17_out, and_6_out, g);
  or or_1 (or_1_out, and_7_out, and_8_out);
  not not_15 (not_15_out, e);
  not not_16 (not_16_out, b);
  and and_18 (and_18_out, and_9_out, g);
  and and_19 (and_19_out, not_12_out, f);
  and and_20 (and_20_out, b, not_13_out);
  and and_21 (and_21_out, and_10_out, and_11_out);
  and and_22 (and_22_out, and_12_out, and_13_out);
  not not_17 (not_17_out, b);
  and and_23 (and_23_out, and_14_out, not_14_out);
  and and_24 (and_24_out, a, d);
  and and_25 (and_25_out, a, b);
  not not_18 (not_18_out, c);
  or or_2 (or_2_out, and_16_out, and_17_out);
  and and_26 (and_26_out, or_1_out, c);
  and and_27 (and_27_out, not_15_out, f);
  not not_19 (not_19_out, g);
  and and_28 (and_28_out, not_16_out, c);
  or or_3 (or_3_out, and_18_out, and_19_out);
  and and_29 (and_29_out, and_20_out, e);
  and and_30 (and_30_out, f, g);
  or or_4 (or_4_out, and_21_out, and_22_out);
  and and_31 (and_31_out, not_17_out, c);
  not not_20 (not_20_out, e);
  or or_5 (or_5_out, and_23_out, and_24_out);
  and and_32 (and_32_out, and_25_out, not_18_out);
  and and_33 (and_33_out, e, or_2_out);
  and and_34 (and_34_out, and_26_out, d);
  and and_35 (and_35_out, and_27_out, not_19_out);
  and and_36 (and_36_out, and_28_out, or_3_out);
  and and_37 (and_37_out, and_29_out, and_30_out);
  and and_38 (and_38_out, a, b);
  and and_39 (and_39_out, g, or_4_out);
  and and_40 (and_40_out, and_31_out, not_20_out);
  and and_41 (and_41_out, f, or_5_out);
  and and_42 (and_42_out, and_32_out, and_33_out);
  and and_43 (and_43_out, and_34_out, and_35_out);
  and and_44 (and_44_out, a, d);
  or or_6 (or_6_out, and_36_out, and_37_out);
  and and_45 (and_45_out, and_38_out, and_39_out);
  and and_46 (and_46_out, and_40_out, and_41_out);
  or or_7 (b2, and_42_out, and_43_out);
  and and_47 (b3, and_44_out, or_6_out);
  or or_8 (b4, and_45_out, and_46_out);
endmodule

module full_adder (
  input  b11,
  input  b12,
  input  b13,
  input  b14,
  input  b21,
  input  b22,
  input  b23,
  input  b24,
  output b4,
  output b3,
  output b2,
  output b1,
  output b0
);

  wire adder_1_cout, adder_2_cout, adder_3_cout;

  Adder #(.width(1)) adder_1 (.a(b24), .b(b14), .out(b4), .cout(adder_1_cout));  // open: cin
  Adder #(.width(1)) adder_2 (.a(b23), .b(b13), .out(b3), .cin(adder_1_cout), .cout(adder_2_cout));
  Adder #(.width(1)) adder_3 (.a(b12), .b(b22), .out(b2), .cin(adder_2_cout), .cout(adder_3_cout));
  Adder #(.width(1)) adder_4 (.a(b11), .b(b21), .out(b1), .cin(adder_3_cout), .cout(b0));
endmodule

module test_bit2led (
  input  a,
  input  b,
  input  c,
  input  d,
  input  e
);

  wire raw_s0, raw_s1, raw_s2, raw_s3, raw_s4, raw_s5, raw_s6, raw_s7, reduced_s0, reduced_s1, reduced_s2,
       reduced_s3, reduced_s4, reduced_s5, reduced_s6, reduced_s7;

  raw_bit2led raw (
    .a(a), .b(b), .c(c), .d(d), .e(e), .s0(raw_s0), .s1(raw_s1), .s2(raw_s2), .s3(raw_s3), .s4(raw_s4),
    .s5(raw_s5), .s6(raw_s6), .s7(raw_s7));
  _7_Segment_Display u_7_segment_display_1 (
    .g(raw_s4), .f(raw_s2), .a(raw_s1), .b(raw_s3), .e(raw_s5), .d(raw_s7), .c(raw_s6), .dp(raw_s0));
  bit2led reduced (
    .a(a), .b(b), .c(c), .d(d), .e(e), .s0(reduced_s0), .s1(reduced_s1), .s2(reduced_s2), .s3(reduced_s3),
    .s4(reduced_s4), .s5(reduced_s5), .s6(reduced_s6), .s7(reduced_s7));
  _7_Segment_Display u_7_segment_display_2 (
    .g(reduced_s4), .f(reduced_s2), .a(reduced_s1), .b(reduced_s3), .e(reduced_s5), .d(reduced_s7),
    .c(reduced_s6), .dp(reduced_s0));
endmodule
